# Fritzing sketch rpi_server (saved by Fritzing 0.9.3b)

parts:
  Raspberry_Pi_1 = Raspberry Pi 3 [part_number=RPI-3-V1.2]
  LoRa_Module1 = Ra-01 - LoRa Module SX1278 [part_number=SX1278]
  ANT1 = Antenna
  Q1 = NPN-Transistor [package="SOT-23 [SMD]"]
  F1 = Fan - Ventilador [package=THT]

nets:
  N1: Raspberry_Pi_1.GPIO2, LoRa_Module1.3.3V
  N2: Raspberry_Pi_1.GPIO4, LoRa_Module1.DIO0
  N3: Raspberry_Pi_1.GPIO17, LoRa_Module1.DIO1
  N4: Raspberry_Pi_1.GPIO27, LoRa_Module1.DIO3
  N5: Raspberry_Pi_1.GPIO22, LoRa_Module1.RESET
  N6: Raspberry_Pi_1.GPIO10, LoRa_Module1.MOSI
  N7: Raspberry_Pi_1.GPIO9, LoRa_Module1.MISO
  N8: Raspberry_Pi_1.GPIO11, LoRa_Module1.SCK
  N9: Raspberry_Pi_1.GPIO8, LoRa_Module1.NSS
  N10: Raspberry_Pi_1.GPIO23, Q1.0
  GND: Raspberry_Pi_1.GND, LoRa_Module1.GND, Q1.2
  N11: Raspberry_Pi_1.GPIO18, LoRa_Module1.DIO2
  5V: Raspberry_Pi_1.5V, F1.5V
  N12: LoRa_Module1.ANT, ANT1.antenna_lead
  N13: Q1.1, F1.GND

custom parts:
  Ra-01 - LoRa Module SX1278: The Ra-01 LoRa Module featuring the SX1278 engine by Semtech. Module by AI-Thinker. Module (Ra-01) specifications from: https://www.banggood.com/Ra-01-Smart-Electronics-SX1278-LoRa-Spread-Spectrum-Wireless-Module-Ultra-Far-10KM-433M-p-1130769.html Description: Power supply: DC1.8-3.7V(3.3V) Chip: SX1278 Frequency: 433Mhz Operating temperature: -40~+85°C On Sheild Description (may vary by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
  Fan - Ventilador: Ventilador de 2 pines, se encuentra comunmente en computadoras de escritorio
