# Fritzing sketch stathmos_estiwn_ATHINA (saved by Fritzing 0.9.3b)
breadboards: 1

parts:
  RHT1 = Humidity and Temperature Sensor RHT03
  Adafruit_LPS2X1 = Adafruit-LPS2X
  Εξάρτημα3 = GUVA-S12SD UV Light Sensor
  LoRa_Module1 = Ra-01 - LoRa Module SX1278 [part_number=SX1278]
  Εξάρτημα6 = MicroSD Card Module
  Εξάρτημα5 = Arduino Mega 2560 (Rev3)
  Εξάρτημα7 = Adafruit TSL2591 High Dynamic Range Digital Light Sensor [part_number="Adafruit #1980"]
  PCB2 = RTC_DS1302_module

nets:
  VCC: RHT1.Vcc, Adafruit_LPS2X1.VCC, Εξάρτημα3.5V, Εξάρτημα6.VCC, Εξάρτημα5.5V, Εξάρτημα7.VCC, PCB2.VCC
  N1: RHT1.Data-signal, Εξάρτημα5.D3_PWM
  GND: RHT1.GND_2, Adafruit_LPS2X1.GND, Εξάρτημα3.GND, LoRa_Module1.GND, Εξάρτημα6.GND, Εξάρτημα5.GND, Εξάρτημα7.GND, PCB2.GND
  N2: Adafruit_LPS2X1.SDI/SDA, LoRa_Module1.MOSI, Εξάρτημα6.MOSI, Εξάρτημα5.D51
  N3: Adafruit_LPS2X1.SCK/SCL, LoRa_Module1.SCK, Εξάρτημα6.SCK, Εξάρτημα5.D52
  N4: Adafruit_LPS2X1.SDO/ADR, LoRa_Module1.MISO, Εξάρτημα6.MISO, Εξάρτημα5.D50
  N5: Adafruit_LPS2X1.CS, Εξάρτημα5.D8_PWM
  N6: Εξάρτημα3.Out, Εξάρτημα5.A3
  N7: LoRa_Module1.NSS, Εξάρτημα5.D10_PWM
  3.3V: LoRa_Module1.3.3V, Εξάρτημα5.3V3
  N8: LoRa_Module1.RESET, Εξάρτημα5.D9_PWM
  N9: LoRa_Module1.DIO0, Εξάρτημα5.D2_PWM
  N10: Εξάρτημα6.CS, Εξάρτημα5.D6_PWM
  N11: Εξάρτημα5.SCL, Εξάρτημα7.SCL
  N12: Εξάρτημα5.SDA, Εξάρτημα7.SDA
  N13: Εξάρτημα5.D4_PWM, PCB2.DAT
  N14: Εξάρτημα5.D5_PWM, PCB2.CLK
  N15: Εξάρτημα5.D7_PWM, PCB2.RST

notes:
  red calbe -> vcc(5-3.3V)
  black cable -> GND
  blue cable -> data
  brown cable -> chip select
  yellow cable -> slk(clock)
  orange cable -> miso
  green cable -> mosi
  pink cable-> sc l
  grey cable -> sda
  purple cable -> rst
  ochre cable ->int

custom parts:
  Adafruit-LPS2X: I've got news for you: we're all sitting at the bottom of an ocean of nitrogen, oxygen, and other gasses. Just like a whale would have trouble breathing if it weren't under an ocean of ocean water, we would have a hard time getting oxygen and nitrogen into our lungs if we weren't swimming in it. Because we're used to being under all this air, for us it's relatively normal to us and we don't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
  GUVA-S12SD UV Light Sensor: Extend your light-sensing spectrum with this analog UV sensor module. It uses a UV photodiode, which can detect the 240-370nm range of light (which covers UVB and most of UVA spectrum). The signal level from the photodiode is very small, in the nano-ampere level, so we tossed on an opamp to amplify the signal to a more manageable volt-level.
  Ra-01 - LoRa Module SX1278: The Ra-01 LoRa Module featuring the SX1278 engine by Semtech. Module by AI-Thinker. Module (Ra-01) specifications from: https://www.banggood.com/Ra-01-Smart-Electronics-SX1278-LoRa-Spread-Spectrum-Wireless-Module-Ultra-Far-10KM-433M-p-1130769.html Description: Power supply: DC1.8-3.7V(3.3V) Chip: SX1278 Frequency: 433Mhz Operating temperature: -40~+85°C On Sheild Description (may vary by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
  Adafruit TSL2591 High Dynamic Range Digital Light Sensor: When the future is dazzlingly-bright, this ultra-high-range luminosity sensor will help you measure it. The TSL2591 luminosity sensor is an advanced digital light sensor, ideal for use in a wide range of light situations. Compared to low cost CdS cells, this sensor is more precise, allowing for exact lux calculations and can be configured for different gain/timing ranges to detect light ranges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
  RTC_DS1302_module: Arduino module DS1302 SPI Real Time Clock
